# Fritzing sketch Wiring (saved by Fritzing 0.9.0b)
breadboards: 1

parts:
  Netduino_1 = Netduino 2
  IC2 = H-Bridge [package=THT]
  M1 = DC Motor
  M2 = DC Motor
  VCC1 = 4 x AAA Battery Mount
  BLE_Mini1 = BLE Mini

nets:
  GND: Netduino_1.GND, IC2.GND1, IC2.GND2, IC2.GND3, IC2.GND4, VCC1.-, BLE_Mini1.GND
  N1: Netduino_1.D8, BLE_Mini1.RX
  N2: Netduino_1.D7, BLE_Mini1.TX
  N3: Netduino_1.D6, IC2.3_4EN
  N4: Netduino_1.D5, IC2.4A
  N5: Netduino_1.D4, IC2.3A
  N6: Netduino_1.D3, IC2.1_2EN
  N7: Netduino_1.D2, IC2.1A
  N8: Netduino_1.D1, IC2.2A
  +5V: Netduino_1.+5V, IC2.VCC1, BLE_Mini1.VIN
  N9: Netduino_1.VIN, IC2.VCC2, VCC1.+
  N10: IC2.1Y, M2.pin_1
  N11: IC2.2Y, M2.pin_2
  N12: IC2.3Y, M1.pin_2
  N13: IC2.4Y, M1.pin_1

custom parts:
  Netduino 2: An open-source electronics platform using the .NET Micro Framework
  BLE Mini: RedBear Labs BLE Mini
